// Logisim project Logique.circ as structural Verilog: 1 circuit, main circuit ACAR
module ACAR (
  input  A,
  input  D,
  input  B,
  input  C
);

  wire not_1_out, not_2_out, or_1_out, or_2_out;

  LED Moteur_droite (.in(not_1_out));
  not not_1 (not_1_out, or_1_out);
  or or_1 (or_1_out, A, B);
  LED Moteur_gauche (.in(not_2_out));
  not not_2 (not_2_out, or_2_out);
  or or_2 (or_2_out, C, D);

  // Notes on the sheet:
  //   0 = Arrière
  //   1 = Avant
  //   Sens des moteurs :
endmodule
